# Fritzing sketch RGB_PCB_esp8266_03 (saved by Fritzing 0.9.3b)
circuit board: 7.07429cm x 4.2079cm

parts:
  7805 = Voltage Regulator - 5V [package="TO220 [THT]"]
  LM117_3_3v = Voltage Regulator - 5V [package="TO220 [THT]"]
  IRLZ44N = Basic FET P-Channel [package="TO220 [THT]"]
  IRLZ44N_2 = Basic FET P-Channel [package="TO220 [THT]"]
  IRLZ44N_3 = Basic FET P-Channel [package="TO220 [THT]"]
  12V = Screw terminal - 2 pins [package=THT]
  2N3904 = NPN-Transistor [package="TO92 [THT]"]
  OUT = screw terminal, 4 pins
  2N3904_2 = NPN-Transistor [package="TO92 [THT]"]
  2N3904_3 = NPN-Transistor [package="TO92 [THT]"]
  10K = Resistor [tolerance=±5% resistance=10k package=THT]
  10k = Resistor [tolerance=±5% resistance=220 package=THT]
  10k_2 = Resistor [tolerance=±5% resistance=220 package=THT]
  1K = Resistor [tolerance=±5% resistance=220 package=THT]
  1K_2 = Resistor [tolerance=±5% resistance=220 package=THT]
  1K_3 = Resistor [tolerance=±5% resistance=220 package=THT]
  0 = Resistor [tolerance=±5% resistance=220 package=THT]
  0_2 = Resistor [tolerance=±5% resistance=220 package=THT]
  10k_3 = Resistor [tolerance=±5% resistance=220 package=THT]
  Pulsador = mystery part, 2 pins [chip_label=?]
  U1 = ESP8266 WiFi Module [part_number=ESP8266]
  0_3 = Resistor [tolerance=±5% resistance=220 package=THT]
  330 = Resistor [tolerance=±5% resistance=220 package=THT]
  WiFiLed = LED - 5mm [color="Red (633nm)" package="5 mm [THT]"]

nets:
  N1: 7805.input_voltage, 12V.pin2, OUT.pin4
  N2: 7805.GND, LM117_3_3v.input_voltage, IRLZ44N.source, IRLZ44N_2.source, IRLZ44N_3.source, 12V.pin1, 0_3.Pin_0
  N3: 7805.output_voltage, LM117_3_3v.output_voltage, 1K.Pin_0, 1K_2.Pin_0, 1K_3.Pin_0
  N4: LM117_3_3v.GND, 10K.Pin_0, 10k.Pin_0, 10k_2.Pin_0, 10k_3.Pin_0, U1.ANT, U1.GPIO_14
  N5: IRLZ44N.gate, 2N3904.C, 1K.Pin_1
  N6: IRLZ44N.drain, 0_2.Pin_0
  N7: IRLZ44N_2.gate, 2N3904_2.C, 1K_2.Pin_1
  N8: IRLZ44N_2.drain, 0.Pin_0
  N9: IRLZ44N_3.gate, 2N3904_3.C, 1K_3.Pin_1
  N10: IRLZ44N_3.drain, OUT.pin1
  N11: 2N3904.E, U1.GPIO_12
  N12: 2N3904.B, 10k.Pin_1
  N13: OUT.pin2, 0.Pin_1
  N14: OUT.pin3, 0_2.Pin_1
  N15: 2N3904_2.E, U1.NC
  N16: 2N3904_2.B, 10k_2.Pin_1
  N17: 2N3904_3.E, U1.GND
  N18: 2N3904_3.B, 10K.Pin_1
  N19: 10k_3.Pin_1, Pulsador.pin2, U1.CH_PD
  N20: Pulsador.pin1, U1.GPIO_0, U1.TXD, 0_3.Pin_1, WiFiLed.cathode
  N21: U1.RXD, 330.Pin_0
  N22: 330.Pin_1, WiFiLed.anode

notes:
  B
  R
  G
  +
  RGB Homekit By Lisergio
  -

custom parts:
  ESP8266 WiFi Module: Generic WiFi Module based on the ESP8266 with onboard PCB antenna and UART communications
